# Fritzing sketch Switcher (saved by Fritzing 0.9.2b)
breadboards: 1

parts:
  R1 = Resistor [tolerance=±5% resistance=10 package=THT]
  Up = PNP-Transistor [package="TO92 [THT]"]
  Down = NPN-Transistor [package="TO92 [THT]"]
  R2 = Resistor [tolerance=±5% resistance=10 package=THT]
  Q1 = NPN-Transistor [package="TO92 [THT]"]
  R4 = Resistor [tolerance=±5% resistance=4k package=THT]
  R5 = Resistor [tolerance=±5% resistance=1k package=THT]
  R6 = Resistor [tolerance=±5% resistance=1k package=THT]
  R7 = Resistor [tolerance=±5% resistance=5k package=THT]
  U1 = CNZ1120 [package=cnz1120]

nets:
  N1: R1.Pin_0, Down.C
  12V out: R1.Pin_1, R2.Pin_1
  12V: Up.E, R4.Pin_0
  N2: Up.B, R7.Pin_1
  N3: Up.C, R2.Pin_0
  GND: Down.E, Q1.E, U1.2, U1.4
  N4: Down.B, R6.Pin_1
  N5: Q1.B, U1.3
  N6: Q1.C, R4.Pin_1, R6.Pin_0, R7.Pin_0
  5V in: R5.Pin_0
  N7: R5.Pin_1, U1.1
