# Fritzing sketch Switcher2 (saved by Fritzing 0.9.2b)
circuit board: 5.31195cm x 2.49059cm
breadboards: 1

parts:
  ADuM5230 = SO16 [chip_label=ADuM5230 package=SO]
  20V = Tantalum Capacitor [capacitance="1 μF" voltage=20V part_number=T491B475K020AT package="B 3528 [SMD, tantalum]"]
  5k = Resistor [tolerance=±5% resistance=5k package="2010 [SMD]"]
  10V = Tantalum Capacitor [capacitance="1 μF" voltage=10V part_number=F931A156MBA package="B 3528 [SMD, tantalum]"]
  10V_2 = Tantalum Capacitor [voltage=10V part_number=F931A156MBA capacitance="1 μF" package="B 3528 [SMD, tantalum]"]
  J1 = female pin header, 3 pins [form="♀ (female)"]
  PNP = PNP-Transistor [package="SOT-23 [SMD]"]
  NPN = NPN-Transistor [package="SOT-23 [SMD]"]
  N-MOSFET = MOSFET-NCHANNEL [package=to220v]
  Vin = female pin header, 1 pin [form="♀ (female)"]
  Vout = female pin header, 1 pin [form="♀ (female)"]

nets:
  GND: ADuM5230.1, ADuM5230.8, 10V.-, 10V_2.-, J1.pin3
  5V: ADuM5230.2, ADuM5230.7, 10V.+, 10V_2.+, J1.pin2
  N1: ADuM5230.5, J1.pin1
  N2: ADuM5230.14, 20V.-, PNP.1, N-MOSFET.S, Vout.pin1
  Viso: ADuM5230.15, 20V.+, NPN.1
  N3: ADuM5230.16, 5k.Pin_0
  N4: 5k.Pin_1, PNP.0, NPN.0
  N5: PNP.2, NPN.2, N-MOSFET.G
  600V: N-MOSFET.D, Vin.pin1

notes:
  5V
  I/O
  GND
  High-side switch
  700V MAX
  Will Yager
  github.com/wyager/Physics
