# Fritzing sketch NID (saved by Fritzing 0.9.2b)
circuit board: 5.21407cm x 2.81516cm
breadboards: 1

parts:
  33pF = Capacitor [part_number=490-7067-ND package=cap-pth-large]
  1MΩ = Resistor [tolerance=±5% resistance=1M power=250mW part_number=1MAACT-ND package=THT]
  Collector = female pin header, 1 pin [form="♀ (female)"]
  HV = female pin header, 2 pins [form="♀ (female)"]
  GND = female pin header, 2 pins [form="♀ (female)"]
  GND_2 = female pin header, 1 pin [form="♀ (female)"]
  Out = female pin header, 1 pin [form="♀ (female)"]
  MOUNT = female pin header, 1 pin [form="♀ (female)"]
  MOUNT1 = female pin header, 1 pin [form="♀ (female)"]

nets:
  N1: 33pF.1, Out.pin1
  N2: 33pF.2, 1MΩ.Pin_1, Collector.pin1
  N3: 1MΩ.Pin_0, HV.pin1, HV.pin2
  GND: GND.pin1, GND.pin2, GND_2.pin1, MOUNT.pin1, MOUNT1.pin1

notes:
  Will Yager
  HV Ion detector filter
