# Fritzing sketch Driver (saved by Fritzing 0.9.2b)
circuit board: 5.56579cm x 1.4972cm
breadboards: 1

parts:
  NPN = NPN-Transistor [package="TO92 [THT]"]
  PNP = PNP-Transistor [package="TO92 [THT]"]
  5K = Resistor [tolerance=±5% resistance=4.7k package=THT]
  FLYBACK = Rectifier Diode [part_number=1N4001 package="300 mil [THT]"]
  1K = Resistor [tolerance=±5% resistance=1k package=THT]
  50V = Electrolytic Capacitor [capacitance=100µF voltage=50V package="100 mil [THT, electrolytic]"]
  OUT = female pin header, 1 pin [form="♀ (female)"]
  GND = female pin header, 1 pin [form="♀ (female)"]
  GND_2 = female pin header, 1 pin [form="♀ (female)"]
  IN = female pin header, 1 pin [form="♀ (female)"]
  30V = female pin header, 1 pin [form="♀ (female)"]
  GND_3 = female pin header, 1 pin [form="♀ (female)"]
  5K_2 = Resistor [tolerance=±5% resistance=4.7k package=THT]
  DISSIPATOR = Resistor [tolerance=±5% resistance=100 package=THT]

nets:
  GND: NPN.E, 50V.-, GND.pin1, GND_2.pin1, GND_3.pin1, DISSIPATOR.Pin_1
  N1: NPN.B, 1K.Pin_1
  N2: NPN.C, 5K_2.Pin_0
  30V: PNP.E, 5K.Pin_1, 50V.+, 30V.pin1
  N3: PNP.B, 5K.Pin_0, 5K_2.Pin_1
  OUT: PNP.C, FLYBACK.cathode, OUT.pin1
  N4: FLYBACK.anode, DISSIPATOR.Pin_0
  IN: 1K.Pin_0, IN.pin1

notes:
  Coil Driver
  Will Yager
  TTL
